# Fritzing sketch asli_oyku_fritzing (saved by Fritzing 1.0.3b)
breadboards: 1

parts:
  Parça1 = RFID-RC522-v2
  U1 = ESP32S-HiLetgo [part_number=ESP32S-HiLetgo]
  U2 = ESP32S-HiLetgo [part_number=ESP32S-HiLetgo]
  LED2 = RGB LED (com. cathode, rbg) [color="Red (633nm)" current=0.030A package="5 mm [THT]"]
  J1 = Basic Servo
  HC-SR04_Sensor_1 = HC-SR04 Ultrasonic Distance Sensor

nets:
  N1: Parça1.SDA, U2.GPIO5
  N2: Parça1.SCK, U2.GPIO18
  N3: Parça1.MOSI, U2.GPIO23
  N4: Parça1.MISO, U2.GPIO19
  GND: Parça1.GND, U1.GND, U2.GND, LED2.common_cathode, J1.gnd, HC-SR04_Sensor_1.GND
  N5: Parça1.RST, U2.GPIO2
  VCC: Parça1.3.3V, U1.3.3, U2.3.3, J1.vcc, HC-SR04_Sensor_1.VCC
  N6: U2.GPIO32, HC-SR04_Sensor_1.ECHO
  N7: U2.GPIO33, HC-SR04_Sensor_1.TRIG
  N8: U2.GPIO25, LED2.red_anode
  N9: U2.GPIO26, LED2.blue_anode
  N10: U2.GPIO27, LED2.green_anode
  N11: U2.GPIO4, J1.pulse

custom parts:
  RFID-RC522-v2: A simple China made RFID-RC522 Reader; do check the pin labels, as this is a MFRC522 based clone.
  ESP32S-HiLetgo: HiLetgo ESP-WROOM-32 ESP32 ESP-32S Development Board 2.4GHz Dual-Mode WiFi + Bluetooth Dual Cores Microcontroller The ESP32 integrated with Antenna switches, RF Balun, power amplifiers, low-noise amplifiers, filters, and management modules, and the entire solution occupies the least area of PCB. 2.4 GHz Wi-Fi plus Bluetooth dual-mode chip, with TSMC Ultra-low power consumption 40nm technology,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
